# Fritzing sketch automatic-watering (saved by Fritzing 0.9.1b)
breadboards: 1

parts:
  M1 = DC Motor
  Parte1 = Arduino Nano (Rev3.0)
  Q1 = NPN-Transistor [package="TO92 [THT]"]
  U1 = HIH-4030 [package=hih-4030]
  U2 = SWITCH_SPDT [package=kps-1290]

nets:
  GND: M1.pin_1, Parte1.GND, U1.GND, U2.P
  N1: M1.pin_2, Q1.C
  N2: Parte1.D4, U2.O
  N3: Parte1.D9, Q1.B
  N4: Parte1.5V, Q1.E
  N5: Parte1.A0, U1.OUT
  3V3: Parte1.3V3, U1.VCC
